// Logisim project GrayZaehler.circ as structural Verilog: 1 circuit, main circuit main
module main (
);

  wire and_1_out, button_1_out, clock_1_out, d_ff_1_q, d_ff_2_q, d_ff_3_q, nand_1_out, nand_2_out,
       nand_3_out, nand_4_out, nand_5_out, nand_6_out, nand_7_out, nand_8_out, nand_9_out, nand_10_out,
       not_1_out, not_2_out, not_3_out, not_4_out, not_5_out, not_6_out, not_7_out, not_8_out, or_1_out,
       or_2_out, or_3_out, or_4_out, q0Q1_2_out, q0Q1_out, q0q1Q2_out, Q0q2_out, Q1Q2_2_out, q1q2_out,
       Q2q3_out, Q3q0_2_out, Q3q0_out;

  Clock clock_1 (.out(clock_1_out));
  nand nand_1 (nand_1_out, clock_1_out, nand_2_out);
  not not_1 (not_1_out, nand_2_out);
  LED led_1 (.in(d_ff_3_q));
  LED led_2 (.in(d_ff_2_q));
  Button button_1 (.out(button_1_out));
  not not_2 (not_2_out, clock_1_out);
  nand nand_2 (nand_2_out, nand_1_out, not_2_out);
  LED led_3 (.in(d_ff_1_q));
  LED led_4 (.in(nand_9_out));
  not not_3 (not_3_out, button_1_out);
  not not_4 (not_4_out, nand_9_out);
  not not_5 (not_5_out, d_ff_1_q);
  not not_6 (not_6_out, d_ff_2_q);
  not not_7 (not_7_out, d_ff_3_q);
  and q1q2 (q1q2_out, not_6_out, not_5_out);
  and Q1Q2_2 (Q1Q2_2_out, d_ff_2_q, d_ff_2_q, d_ff_1_q);
  and Q3q0 (Q3q0_out, d_ff_3_q, not_4_out);
  and q0Q1 (q0Q1_out, d_ff_1_q, not_4_out);
  and Q0q2 (Q0q2_out, nand_9_out, not_6_out);
  and Q2q3 (Q2q3_out, not_7_out, d_ff_2_q);
  and Q3q0_2 (Q3q0_2_out, d_ff_3_q, d_ff_3_q, not_4_out);
  and q0Q1_2 (q0Q1_2_out, not_4_out, d_ff_1_q);
  and q0q1Q2 (q0q1Q2_out, d_ff_2_q, not_5_out, not_4_out);
  or or_1 (or_1_out, q1q2_out, Q1Q2_2_out, Q3q0_out);
  or or_2 (or_2_out, q0Q1_out, Q0q2_out);
  or or_3 (or_3_out, Q2q3_out, Q3q0_2_out, Q3q0_2_out, q0Q1_2_out);
  not not_8 (not_8_out, or_1_out);
  D_Flip_Flop d_ff_1 (.clk(not_1_out), .D(or_2_out), .Q(d_ff_1_q), .reset(button_1_out));  // open: Qn, preset, en
  D_Flip_Flop d_ff_2 (.clk(not_1_out), .D(or_3_out), .Q(d_ff_2_q), .reset(button_1_out));  // open: Qn, preset, en
  D_Flip_Flop d_ff_3 (.clk(not_1_out), .D(q0q1Q2_out), .Q(d_ff_3_q), .reset(button_1_out));  // open: Qn, preset, en
  nand nand_3 (nand_3_out, or_1_out, not_1_out);
  nand nand_4 (nand_4_out, not_8_out, not_1_out);
  nand nand_5 (nand_5_out, nand_3_out, nand_6_out);
  nand nand_6 (nand_6_out, nand_5_out, nand_4_out);
  nand nand_7 (nand_7_out, nand_5_out, nand_2_out);
  nand nand_8 (nand_8_out, nand_2_out, nand_6_out);
  or or_4 (or_4_out, nand_7_out, button_1_out);
  and and_1 (and_1_out, nand_8_out, not_3_out);
  nand nand_9 (nand_9_out, or_4_out, nand_10_out);
  nand nand_10 (nand_10_out, nand_9_out, and_1_out);

  // Notes on the sheet:
  //   Entpreller
  //   Q3
  //   Q2
  //   Q1
  //   Gray Code Ausgabe
  //   Reset
  //   Q0
  //   q0
  //   q1
  //   q2
  //   q3
  //   D1
  //   D2
  //   D3
  //   D0
  //   Master RS FF
  //   Slave RS FF
endmodule
