// Logisim project MasterSlaveDFF.circ as structural Verilog: 1 circuit, main circuit main
module main (
  input  in_1
);

  wire and_1_out, button_1_out, clock_1_out, nand_1_out, nand_2_out, nand_3_out, nand_4_out, nand_5_out,
       nand_6_out, nand_7_out, nand_8_out, not_1_out, not_2_out, not_3_out, or_1_out;

  not not_1 (not_1_out, clock_1_out);
  Clock clock_1 (.out(clock_1_out));
  LED led_1 (.in(clock_1_out));
  LED led_2 (.in(in_1));
  not not_2 (not_2_out, in_1);
  nand nand_1 (nand_1_out, in_1, not_1_out);
  nand nand_2 (nand_2_out, not_1_out, not_2_out);
  nand nand_3 (nand_3_out, nand_1_out, nand_4_out);
  nand nand_4 (nand_4_out, nand_3_out, nand_2_out);
  Button button_1 (.out(button_1_out));
  nand nand_5 (nand_5_out, nand_3_out, clock_1_out);
  not not_3 (not_3_out, button_1_out);
  nand nand_6 (nand_6_out, clock_1_out, nand_4_out);
  or or_1 (or_1_out, button_1_out, nand_5_out);
  and and_1 (and_1_out, not_3_out, nand_6_out);
  nand nand_7 (nand_7_out, or_1_out, nand_8_out);
  nand nand_8 (nand_8_out, nand_7_out, and_1_out);
  _7_Segment_Display u_7_segment_display_1 (
    .f(nand_3_out), .a(not_1_out), .b(nand_7_out), .e(nand_4_out), .d(clock_1_out), .c(nand_8_out));  // open: g, dp
endmodule
