// Logisim project Versuch3_Augabe3.circ as structural Verilog: 1 circuit, main circuit main
module main (
);

  wire and_1_out, and_2_out, and_3_out, and_4_out, and_5_out, and_6_out, and_7_out, and_8_out, and_9_out,
       and_10_out, and_11_out, and_12_out, and_13_out, and_14_out, and_15_out, and_16_out, and_17_out,
       button_1_out, clock_1_out, d_ff_1_q, d_ff_2_q, d_ff_3_q, nand_1_out, nand_2_out, nand_3_out,
       nand_4_out, nand_5_out, nand_6_out, nand_7_out, nand_8_out, nand_9_out, nand_10_out, not_1_out,
       not_2_out, not_3_out, not_4_out, not_5_out, not_6_out, or_1_out, or_2_out, or_3_out, or_4_out,
       or_5_out, or_6_out, or_7_out, or_8_out, or_9_out, or_10_out;

  Clock clock_1 (.out(clock_1_out));
  not not_1 (not_1_out, clock_1_out);
  Button button_1 (.out(button_1_out));
  _7_Segment_Display u_7_segment_display_1 (
    .g(or_9_out), .f(or_10_out), .a(or_1_out), .b(or_2_out), .e(or_5_out), .d(or_4_out), .c(or_3_out));  // open: dp
  nand nand_1 (nand_1_out, clock_1_out, nand_2_out);
  nand nand_2 (nand_2_out, nand_1_out, not_1_out);
  not not_2 (not_2_out, nand_2_out);
  not not_3 (not_3_out, d_ff_1_q);
  not not_4 (not_4_out, nand_9_out);
  not not_5 (not_5_out, d_ff_2_q);
  not not_6 (not_6_out, d_ff_3_q);
  and and_1 (and_1_out, nand_9_out, d_ff_2_q);
  and and_2 (and_2_out, not_4_out, not_5_out);
  and and_3 (and_3_out, nand_9_out, d_ff_1_q);
  and and_4 (and_4_out, not_4_out, not_3_out);
  and and_5 (and_5_out, not_4_out, d_ff_1_q);
  and and_6 (and_6_out, d_ff_1_q, not_5_out);
  and and_7 (and_7_out, not_3_out, d_ff_2_q);
  and and_8 (and_8_out, not_4_out, d_ff_2_q);
  and and_9 (and_9_out, nand_9_out, not_3_out, d_ff_2_q);
  nand nand_3 (nand_3_out, not_4_out, not_2_out);
  nand nand_4 (nand_4_out, not_2_out, nand_9_out);
  or or_1 (or_1_out, and_1_out, and_2_out, d_ff_1_q, not_6_out);
  nand nand_5 (nand_5_out, nand_3_out, nand_6_out);
  nand nand_6 (nand_6_out, nand_5_out, nand_4_out);
  or or_2 (or_2_out, and_3_out, and_4_out, not_5_out);
  and and_10 (and_10_out, not_4_out, d_ff_1_q);
  and and_11 (and_11_out, nand_9_out, not_3_out, not_6_out);
  and and_12 (and_12_out, not_4_out, d_ff_2_q);
  and and_13 (and_13_out, not_3_out, d_ff_2_q, not_6_out);
  and and_14 (and_14_out, nand_9_out, d_ff_1_q, not_5_out);
  and and_15 (and_15_out, d_ff_3_q, not_4_out);
  and and_16 (and_16_out, nand_9_out, d_ff_1_q, d_ff_2_q);
  or or_3 (or_3_out, nand_9_out, not_4_out, d_ff_3_q);
  or or_4 (or_4_out, and_2_out, and_5_out, and_6_out, and_9_out, not_6_out);
  nand nand_7 (nand_7_out, nand_5_out, nand_2_out);
  nand nand_8 (nand_8_out, nand_2_out, nand_6_out);
  or or_5 (or_5_out, and_2_out, and_5_out);
  and and_17 (and_17_out, nand_8_out, button_1_out);
  or or_6 (or_6_out, and_10_out, and_11_out);
  or or_7 (or_7_out, and_12_out, and_13_out, and_14_out);
  or or_8 (or_8_out, and_15_out, and_16_out);
  nand nand_9 (nand_9_out, nand_7_out, nand_10_out);
  nand nand_10 (nand_10_out, nand_9_out, and_17_out, and_17_out);
  D_Flip_Flop d_ff_1 (.clk(nand_2_out), .D(or_6_out), .Q(d_ff_1_q));  // open: Qn, preset, en, reset
  D_Flip_Flop d_ff_2 (.clk(nand_2_out), .D(or_7_out), .Q(d_ff_2_q));  // open: Qn, preset, en, reset
  D_Flip_Flop d_ff_3 (.clk(nand_2_out), .D(or_8_out), .Q(d_ff_3_q));  // open: Qn, preset, en, reset
  or or_9 (or_9_out, and_5_out, and_6_out, and_7_out, not_6_out);
  or or_10 (or_10_out, and_4_out, and_7_out, and_8_out, not_6_out);
endmodule
